# Fritzing sketch Project sketch (saved by Fritzing 0.9.10b)
breadboards: 1

parts:
  LCM1602_IIC1 = LCM1602 IIC [part_number="LCM1602 IIC" chip_label="LCM1602 IIC" package="DIP (Dual Inline) [THT]"]
  LCD = LCD screen
  Onderdeel1 = RFID-RC522-v2
  Onderdeel2 = Arduino Uno (Rev3) - ICSP
  Bidirectional_level_shifter = I2C level shifter bidirectional
  WeMos_D1_Mini1 = WeMos D1 Mini  # not connected
  HC-SR04_Sensor_1 = HC-SR04 Ultrasonic Distance Sensor
  Step_motor = 28BYJ-48 Stepper Motor [part_number=28BYJ-48]
  Motor_contoller = 28BYJ-48 Driver Module [part_number=ULN2003 package=THT]

nets:
  VSS: LCM1602_IIC1.VSS, LCD.VSS
  VDD: LCM1602_IIC1.VDD, LCD.VDD
  N1: LCM1602_IIC1.V0, LCD.V0
  N2: LCM1602_IIC1.RS, LCD.RS
  N3: LCM1602_IIC1.RW, LCD.R/W
  N4: LCM1602_IIC1.E, LCD.E
  N5: LCM1602_IIC1.D0, LCD.DB0
  N6: LCM1602_IIC1.D1, LCD.DB1
  N7: LCM1602_IIC1.D2, LCD.DB2
  N8: LCM1602_IIC1.D3, LCD.DB3
  N9: LCM1602_IIC1.D4, LCD.DB4
  N10: LCM1602_IIC1.D5, LCD.DB5
  N11: LCM1602_IIC1.D6, LCD.DB6
  N12: LCM1602_IIC1.D7, LCD.DB7
  N13: LCM1602_IIC1.A, LCD.LED+
  N14: LCM1602_IIC1.K, LCD.LED-
  GND: LCM1602_IIC1.GND, Onderdeel1.GND, Onderdeel2.GND, Bidirectional_level_shifter.GND, HC-SR04_Sensor_1.GND
  VCC: LCM1602_IIC1.VCC, Onderdeel2.5V, Bidirectional_level_shifter.HV, HC-SR04_Sensor_1.VCC
  N15: LCM1602_IIC1.SDA, Onderdeel2.A4/SDA
  N16: LCM1602_IIC1.SCL, Onderdeel2.A5/SCL
  N17: Onderdeel1.SCK, Onderdeel2.D10_PWM/SS
  N18: Onderdeel1.MOSI, Onderdeel2.D13/SCK
  N19: Onderdeel1.MISO, Onderdeel2.D11_PWM/MOSI
  N20: Onderdeel1.IRQ, Onderdeel2.D12/MISO
  N21: Onderdeel1.RST, Onderdeel2.D9_PWM
  N22: Onderdeel1.3_3V, Onderdeel2.3V3
  N23: Onderdeel2.D0/RX, Bidirectional_level_shifter.HV1
  N24: Onderdeel2.D1/TX, Bidirectional_level_shifter.HV2
  N25: Onderdeel2.D2, Motor_contoller.IN4
  N26: Onderdeel2.D3_PWM, Motor_contoller.IN3
  N27: Onderdeel2.D4, Motor_contoller.IN2
  N28: Onderdeel2.D5_PWM, Motor_contoller.IN1
  N29: Onderdeel2.D6_PWM, HC-SR04_Sensor_1.ECHO
  N30: Onderdeel2.D7, HC-SR04_Sensor_1.TRIG
  N31: Step_motor.blue-pin, Motor_contoller.blue-pin
  N32: Step_motor.pink-pin, Motor_contoller.pink-pin
  N33: Step_motor.yellow-pin, Motor_contoller.yellow-pin
  N34: Step_motor.orange-pin, Motor_contoller.orange-pin
  N35: Step_motor.red-pin, Motor_contoller.red-pin

custom parts:
  LCM1602 IIC: I2C-Module to use a 1602 or 2004 LCD on with the wire.h libory Serial LCD Modul
  RFID-RC522-v2: A simple China made RFID-RC522 Reader; do check the pin labels, as this is a MFRC522 based clone.
  28BYJ-48 Stepper Motor: Unipolar Stepper Motor 28BYJ-48 Top coil - pink & orange Bottom coil - blue & yellow Common rail - red Connector pins: blue - pink - yellow - orange - red
  28BYJ-48 Driver Module: Generic male header
